// Logisim project Char_Display_Device.circ as structural Verilog: 1 circuit, main circuit main
module main (
);

  wire _1, _2, _5, _6, _7, _8, _9, _10, _12, _13, _14, _15, _16, _17, _18, _19, _20, _21, _22, _23, _24, _25,
       _26, _27, _28, _29, _30, _31, _32, _33, _35, A0, A1, A2, A6, A8, A9, A11, A12, A14, A15, and_20_out,
       and_21_out, and_22_out, and_23_out, and_24_out, and_25_out, and_26_out, and_27_out, and_28_out,
       and_29_out, and_30_out, and_31_out, and_32_out, and_33_out, and_34_out, and_35_out, and_36_out,
       and_37_out, and_38_out, and_39_out, and_40_out, and_41_out, and_42_out, and_43_out, and_44_out,
       and_45_out, and_46_out, and_47_out, and_48_out, and_49_out, and_50_out, and_51_out, and_52_out,
       and_53_out, and_54_out, and_55_out, and_56_out, and_57_out, and_58_out, and_59_out, and_60_out,
       and_61_out, and_62_out, and_63_out, and_64_out, and_65_out, and_66_out, and_67_out, and_68_out,
       and_69_out, and_70_out, and_71_out, and_72_out, and_73_out, and_74_out, and_75_out, and_76_out,
       and_77_out, and_78_out, and_79_out, and_80_out, and_81_out, and_82_out, and_83_out, and_84_out,
       and_85_out, and_86_out, and_87_out, and_88_out, and_89_out, and_90_out, and_91_out, and_92_out,
       and_93_out, and_94_out, and_95_out, and_96_out, and_97_out, and_98_out, and_99_out, and_100_out,
       and_101_out, and_102_out, and_103_out, and_104_out, and_105_out, and_106_out, and_107_out,
       and_108_out, and_109_out, and_110_out, and_111_out, and_112_out, and_113_out, and_114_out,
       and_115_out, and_116_out, and_117_out, and_118_out, and_119_out, and_120_out, and_121_out,
       and_122_out, and_123_out, and_124_out, and_125_out, and_126_out, and_127_out, and_128_out,
       and_129_out, and_130_out, and_131_out, and_132_out, and_133_out, and_134_out, and_135_out,
       and_136_out, and_137_out, and_138_out, and_139_out, and_140_out, and_141_out, and_142_out,
       and_143_out, and_144_out, and_145_out, and_146_out, and_147_out, and_148_out, and_149_out,
       and_150_out, and_151_out, and_152_out, and_153_out, and_154_out, and_155_out, and_156_out,
       and_157_out, and_158_out, and_159_out, and_160_out, and_161_out, and_162_out, and_163_out,
       and_164_out, and_165_out, and_166_out, and_167_out, and_168_out, and_169_out, and_170_out,
       and_171_out, and_172_out, and_173_out, and_174_out, and_175_out, and_176_out, and_177_out,
       and_178_out, and_179_out, B0, B2, B4, B6, B7, B8, B9, B14, B15, CP, nand_1_out, nand_2_out,
       nand_3_out, nand_4_out, nand_5_out, nand_6_out, nand_7_out, nand_8_out, nand_9_out, not_1_out,
       not_2_out, not_3_out, not_4_out, not_5_out, not_6_out, not_7_out, not_8_out, or_1_out, or_2_out,
       or_3_out, or_4_out, or_5_out, or_6_out, or_7_out, or_8_out, or_9_out, or_10_out, or_11_out, or_12_out,
       or_13_out, or_14_out, or_15_out, or_16_out, or_17_out, or_18_out, or_19_out, or_20_out, or_21_out,
       or_22_out, or_23_out, or_24_out, or_25_out, or_26_out, or_27_out, or_28_out, or_29_out, or_30_out,
       or_31_out, or_32_out, or_33_out, or_34_out, or_35_out, or_36_out, or_37_out, or_38_out, or_39_out,
       or_40_out, or_41_out, or_42_out, or_43_out, or_44_out, or_45_out, or_46_out, or_47_out, or_48_out,
       or_49_out, or_50_out, or_51_out, or_52_out, or_53_out, or_54_out, or_55_out, or_56_out, or_57_out,
       or_58_out, or_59_out, or_60_out, or_61_out, or_62_out, or_63_out, or_64_out, or_65_out, or_66_out,
       or_67_out, or_68_out, or_69_out, or_70_out, or_71_out, or_72_out, or_73_out, or_74_out, or_75_out,
       or_76_out, or_77_out, or_78_out, or_79_out, or_80_out, or_81_out, or_82_out, or_83_out, or_84_out,
       or_85_out, or_86_out, or_87_out, or_88_out, or_89_out, or_90_out, or_91_out, or_92_out, or_93_out,
       or_94_out, or_95_out, or_96_out, or_97_out, or_98_out, or_99_out, or_100_out, or_101_out, or_102_out,
       or_103_out, or_104_out, or_105_out, or_106_out, or_107_out, or_108_out, or_109_out, or_110_out,
       or_111_out, or_112_out, or_113_out;

  not not_1 (not_1_out, _16);
  not not_2 (not_2_out, _17);
  not not_3 (not_3_out, _20);
  not not_4 (not_4_out, _18);
  and and_1 (A1, not_1_out, not_2_out, not_4_out, _20);
  and and_2 (A6, not_1_out, _17, _18, not_3_out);
  and and_3 (A9, _16, not_2_out, not_4_out, _20);
  and and_4 (A12, _16, _17, not_4_out, not_3_out);
  and and_5 (A15, _16, _17, _18, _20);
  and and_6 (A0, not_1_out, not_2_out, not_4_out, not_3_out);
  and and_7 (A2, not_1_out, not_2_out, _18, not_3_out);
  and and_8 (A8, _16, not_2_out, not_4_out, not_3_out);
  and and_9 (A11, _16, not_2_out, _18, _20);
  and and_10 (A14, _16, _17, _18, not_3_out);
  not not_5 (not_5_out, _31);
  not not_6 (not_6_out, _32);
  not not_7 (not_7_out, _33);
  not not_8 (not_8_out, _35);
  and and_11 (B0, not_5_out, not_6_out, not_7_out, not_8_out);
  and and_12 (B2, not_5_out, not_6_out, _33, not_8_out);
  and and_13 (B4, not_5_out, _32, not_7_out, not_8_out);
  and and_14 (B6, not_5_out, _32, _33, not_8_out);
  and and_15 (B7, not_5_out, _32, _33, _35);
  and and_16 (B8, _31, not_6_out, not_7_out, not_8_out);
  and and_17 (B9, _31, not_6_out, not_7_out, _35);
  and and_18 (B14, _31, _32, _33, not_8_out);
  and and_19 (B15, _31, _32, _33, _35);
  Clock clock_1 (.out(CP));
  LED led_1 (.in(_2));
  LED led_2 (.in(_1));
  LED led_3 (.in(_7));
  LED led_4 (.in(_6));
  LED led_5 (.in(_6));
  LED led_6 (.in(_12));
  LED led_7 (.in(_16));
  LED led_8 (.in(_17));
  LED led_9 (.in(_21));
  LED led_10 (.in(_22));
  LED led_11 (.in(_27));
  LED led_12 (.in(_26));
  LED led_13 (.in(_31));
  LED led_14 (.in(_32));
  LED led_15 (.in(_2));
  LED led_16 (.in(_2));
  LED led_17 (.in(_8));
  LED led_18 (.in(_9));
  LED led_19 (.in(_14));
  LED led_20 (.in(_13));
  LED led_21 (.in(_19));
  LED led_22 (.in(_18));
  LED led_23 (.in(_23));
  LED led_24 (.in(_24));
  LED led_25 (.in(_29));
  LED led_26 (.in(_28));
  LED led_27 (.in(_32));
  LED led_28 (.in(_33));
  LED led_29 (.in(_5));
  LED led_30 (.in(_10));
  LED led_31 (.in(_15));
  LED led_32 (.in(_20));
  LED led_33 (.in(_25));
  LED led_34 (.in(_30));
  LED led_35 (.in(_35));
  and and_20 (and_20_out, B0, or_1_out);
  or or_1 (or_1_out, A15, A8, A9);
  and and_21 (and_21_out, B6, or_2_out);
  or or_2 (or_2_out, A1, A8, A6);
  and and_22 (and_22_out, B9, or_3_out);
  or or_3 (or_3_out, A11, A14, A15);
  and and_23 (and_23_out, B8, or_4_out);
  or or_4 (or_4_out, A8, A14);
  or or_5 (or_5_out, A1, A8);
  or or_6 (or_6_out, A11, A15);
  or or_7 (or_7_out, A2, A6);
  or or_8 (or_8_out, A2, A6, A8);
  and and_24 (and_24_out, or_8_out, B6);
  or or_9 (or_9_out, A11, A12, A15);
  and and_25 (and_25_out, or_9_out, B9);
  or or_10 (or_10_out, A2, A8);
  and and_26 (and_26_out, or_10_out, B15);
  or or_11 (or_11_out, A1, A6);
  or or_12 (or_12_out, A2, A6);
  and and_27 (and_27_out, or_12_out, B2);
  or or_13 (or_13_out, A14, A15);
  and and_28 (and_28_out, A2, B2);
  and and_29 (and_29_out, A1, B6);
  and and_30 (and_30_out, A9, B4);
  and and_31 (and_31_out, A0, B0);
  and and_32 (and_32_out, or_5_out, B6);
  and and_33 (and_33_out, A2, B15);
  and and_34 (and_34_out, or_6_out, B9);
  and and_35 (and_35_out, or_7_out, B2);
  and and_36 (and_36_out, A0, B0);
  and and_37 (and_37_out, or_11_out, B6);
  and and_38 (and_38_out, B9, A15);
  and and_39 (and_39_out, A8, B15);
  and and_40 (and_40_out, A9, B9);
  and and_41 (and_41_out, A0, B0);
  and and_42 (and_42_out, or_13_out, B9);
  and and_43 (and_43_out, A15, B0);
  or or_14 (or_14_out, B14, B8, B9);
  or or_15 (or_15_out, B8, B0, B6);
  or or_16 (or_16_out, B0, B7, B4);
  or or_17 (or_17_out, B2, B9);
  or or_18 (or_18_out, A11, A15);
  and and_44 (and_44_out, B15, A2);
  and and_45 (and_45_out, B7, A9);
  and and_46 (and_46_out, B14, A14);
  or or_19 (or_19_out, and_32_out, and_33_out, and_31_out, and_34_out, and_35_out);
  and and_47 (and_47_out, B8, A8);
  and and_48 (and_48_out, B14, A9);
  or or_20 (or_20_out, and_37_out, and_36_out, and_38_out, and_27_out);
  or or_21 (or_21_out, and_39_out, and_40_out);
  or or_22 (or_22_out, and_42_out, and_28_out, and_41_out, and_29_out, and_30_out);
  and and_49 (and_49_out, or_14_out, A14);
  and and_50 (and_50_out, or_15_out, A8);
  and and_51 (and_51_out, or_16_out, A9);
  and and_52 (and_52_out, A1, B6);
  and and_53 (and_53_out, or_17_out, A6);
  and and_54 (and_54_out, or_18_out, B9);
  and and_55 (and_55_out, A2, B15);
  or or_23 (or_23_out, and_20_out, and_21_out, and_44_out, and_45_out, and_46_out, and_22_out, and_23_out);
  T_Flip_Flop t_ff_1 (.clk(CP), .T(or_19_out), .Q(_2));  // open: Qn, preset, reset, en
  or or_24 (or_24_out, and_24_out, and_47_out, and_25_out, and_48_out, and_26_out);
  T_Flip_Flop t_ff_2 (.clk(CP), .T(or_20_out), .Q(_6));  // open: Qn, preset, reset, en
  T_Flip_Flop t_ff_3 (.clk(CP), .T(or_21_out), .Q(_7));  // open: Qn, preset, reset, en
  T_Flip_Flop t_ff_4 (.clk(CP), .T(or_22_out), .Q(_16));  // open: Qn, preset, reset, en
  or or_25 (or_25_out, and_43_out, and_49_out, and_50_out, and_51_out, and_53_out, and_54_out, and_55_out, and_52_out);
  T_Flip_Flop t_ff_5 (.clk(CP), .T(or_23_out), .Q(_1));  // open: Qn, preset, reset, en
  T_Flip_Flop t_ff_6 (.clk(CP), .T(or_24_out), .Q(_5));  // open: Qn, preset, reset, en
  T_Flip_Flop t_ff_7 (.clk(CP), .T(or_25_out), .Q(_31));  // open: Qn, preset, reset, en
  or or_26 (or_26_out, A2, A6);
  and and_56 (and_56_out, A0, B0);
  or or_27 (or_27_out, A1, A2, A6);
  and and_57 (and_57_out, B14, A9);
  and and_58 (and_58_out, A8, B8);
  or or_28 (or_28_out, A2, A8);
  or or_29 (or_29_out, A9, A11);
  and and_59 (and_59_out, B8, A8);
  or or_30 (or_30_out, A8, A14);
  and and_60 (and_60_out, A8, B8);
  or or_31 (or_31_out, A9, A12, A15);
  and and_61 (and_61_out, or_31_out, B9);
  and and_62 (and_62_out, A2, B2);
  or or_32 (or_32_out, A1, A2, A6);
  and and_63 (and_63_out, or_32_out, B6);
  or or_33 (or_33_out, B2, B6);
  and and_64 (and_64_out, A15, B9);
  and and_65 (and_65_out, or_26_out, B6);
  and and_66 (and_66_out, B2, A2);
  and and_67 (and_67_out, A8, B15);
  or or_34 (or_34_out, A9, A12);
  and and_68 (and_68_out, or_34_out, B9);
  and and_69 (and_69_out, A1, B6);
  and and_70 (and_70_out, or_27_out, B6);
  and and_71 (and_71_out, A2, B2);
  and and_72 (and_72_out, B9, A15);
  and and_73 (and_73_out, or_28_out, B15);
  and and_74 (and_74_out, B15, A14);
  and and_75 (and_75_out, or_29_out, B9);
  and and_76 (and_76_out, or_30_out, B15);
  or or_35 (or_35_out, B8, B14, B15);
  or or_36 (or_36_out, B0, B4, B7, B14);
  and and_77 (and_77_out, or_33_out, A6);
  and and_78 (and_78_out, A12, B9);
  and and_79 (and_79_out, A14, B14);
  or or_37 (or_37_out, A1, A8, A9, A6);
  or or_38 (or_38_out, A15, A12, A14);
  or or_39 (or_39_out, A14, A8, A2);
  or or_40 (or_40_out, A2, A9, A6);
  or or_41 (or_41_out, A8, A15);
  or or_42 (or_42_out, A8, A14);
  or or_43 (or_43_out, B4, B7);
  or or_44 (or_44_out, and_64_out, and_65_out, and_66_out);
  or or_45 (or_45_out, and_67_out, and_68_out, and_69_out);
  or or_46 (or_46_out, and_70_out, and_57_out, and_71_out, and_56_out, and_58_out, and_72_out, and_73_out);
  or or_47 (or_47_out, and_74_out, and_75_out, and_59_out);
  or or_48 (or_48_out, and_76_out, and_60_out, and_61_out, and_62_out, and_63_out);
  and and_80 (and_80_out, A0, B0);
  and and_81 (and_81_out, or_35_out, A14);
  and and_82 (and_82_out, A8, B6);
  and and_83 (and_83_out, or_36_out, A9);
  and and_84 (and_84_out, A15, B9);
  and and_85 (and_85_out, A1, B6);
  and and_86 (and_86_out, or_37_out, B6);
  and and_87 (and_87_out, or_38_out, B9);
  and and_88 (and_88_out, or_39_out, B15);
  and and_89 (and_89_out, or_40_out, B2);
  and and_90 (and_90_out, or_41_out, B0);
  and and_91 (and_91_out, or_42_out, B8);
  and and_92 (and_92_out, or_43_out, A9);
  T_Flip_Flop t_ff_8 (.clk(CP), .T(or_44_out), .Q(_8));  // open: Qn, preset, reset, en
  T_Flip_Flop t_ff_9 (.clk(CP), .T(or_45_out), .Q(_9));  // open: Qn, preset, reset, en
  T_Flip_Flop t_ff_10 (.clk(CP), .T(or_46_out), .Q(_10));  // open: Qn, preset, reset, en
  T_Flip_Flop t_ff_11 (.clk(CP), .T(or_47_out), .Q(_12));  // open: Qn, preset, reset, en
  T_Flip_Flop t_ff_12 (.clk(CP), .T(or_48_out), .Q(_13));  // open: Qn, preset, reset, en
  or or_49 (or_49_out, and_80_out, and_81_out, and_82_out, and_83_out, and_77_out, and_85_out, and_78_out, and_84_out);
  or or_50 (or_50_out, and_79_out, and_86_out, and_87_out, and_88_out, and_90_out, and_91_out, and_92_out, and_89_out);
  T_Flip_Flop t_ff_13 (.clk(CP), .T(or_49_out), .Q(_17));  // open: Qn, preset, reset, en
  T_Flip_Flop t_ff_14 (.clk(CP), .T(or_50_out), .Q(_32));  // open: Qn, preset, reset, en
  or or_51 (or_51_out, A9, A14);
  or or_52 (or_52_out, A1, A2, A8);
  or or_53 (or_53_out, A14, A15);
  or or_54 (or_54_out, A2, A6);
  and and_93 (and_93_out, A6, B2);
  or or_55 (or_55_out, A2, A14);
  and and_94 (and_94_out, A8, B8);
  and and_95 (and_95_out, or_51_out, B14);
  and and_96 (and_96_out, B0, A8);
  and and_97 (and_97_out, or_52_out, B6);
  and and_98 (and_98_out, A8, B15);
  and and_99 (and_99_out, or_53_out, B9);
  and and_100 (and_100_out, or_54_out, B2);
  or or_56 (or_56_out, B8, B14, B15);
  or or_57 (or_57_out, B2, B6);
  or or_58 (or_58_out, B0, B4, B7, B14);
  or or_59 (or_59_out, A14, A6, A15);
  and and_101 (and_101_out, A2, B2);
  and and_102 (and_102_out, A1, B6);
  or or_60 (or_60_out, A12, A15, A14, A6);
  or or_61 (or_61_out, A14, A8, A2);
  and and_103 (and_103_out, or_55_out, B15);
  or or_62 (or_62_out, and_93_out, and_103_out, and_94_out);
  and and_104 (and_104_out, A0, B0);
  and and_105 (and_105_out, A0, B0);
  and and_106 (and_106_out, or_56_out, A14);
  and and_107 (and_107_out, A15, B9);
  and and_108 (and_108_out, or_57_out, A6);
  and and_109 (and_109_out, A8, B6);
  and and_110 (and_110_out, or_58_out, A9);
  and and_111 (and_111_out, or_59_out, B9);
  and and_112 (and_112_out, A0, B0);
  or or_63 (or_63_out, B8, B14, B15);
  and and_113 (and_113_out, A14, B14);
  and and_114 (and_114_out, or_60_out, B9);
  and and_115 (and_115_out, or_61_out, B15);
  or or_64 (or_64_out, A15, A8);
  and and_116 (and_116_out, or_64_out, B0);
  or or_65 (or_65_out, A8, A14);
  and and_117 (and_117_out, or_65_out, B8);
  or or_66 (or_66_out, A8, A1);
  and and_118 (and_118_out, or_66_out, B6);
  or or_67 (or_67_out, B2, B7);
  and and_119 (and_119_out, or_67_out, A9);
  T_Flip_Flop t_ff_15 (.clk(CP), .T(or_62_out), .Q(_14));  // open: Qn, preset, reset, en
  or or_68 (or_68_out, and_95_out, and_96_out, and_97_out, and_104_out, and_98_out, and_99_out, and_100_out);
  or or_69 (or_69_out, and_105_out, and_106_out, and_107_out, and_109_out, and_110_out, and_108_out);
  or or_70 (or_70_out, and_111_out, and_101_out, and_102_out, and_112_out);
  and and_120 (and_120_out, or_63_out, A14);
  and and_121 (and_121_out, A11, B9);
  or or_71 (or_71_out, B0, B4, B7, B9, B14);
  and and_122 (and_122_out, or_71_out, A9);
  or or_72 (or_72_out, B2, B6, B15);
  T_Flip_Flop t_ff_16 (.clk(CP), .T(or_68_out), .Q(_15));  // open: Qn, preset, reset, en
  T_Flip_Flop t_ff_17 (.clk(CP), .T(or_69_out), .Q(_19));  // open: Qn, preset, reset, en
  T_Flip_Flop t_ff_18 (.clk(CP), .T(or_70_out), .Q(_21));  // open: Qn, preset, reset, en
  and and_123 (and_123_out, A0, B0);
  and and_124 (and_124_out, A8, B6);
  and and_125 (and_125_out, or_72_out, A2);
  or or_73 (or_73_out, and_114_out, and_115_out, and_116_out, and_113_out, and_117_out, and_118_out, and_119_out);
  or or_74 (or_74_out, and_123_out, and_120_out, and_121_out, and_124_out, and_125_out, and_122_out);
  T_Flip_Flop t_ff_19 (.clk(CP), .T(or_73_out), .Q(_33));  // open: Qn, preset, reset, en
  T_Flip_Flop t_ff_20 (.clk(CP), .T(or_74_out), .Q(_18));  // open: Qn, preset, reset, en
  and and_126 (and_126_out, A6, B2);
  and and_127 (and_127_out, A2, B15);
  or or_75 (or_75_out, A6, A12, A14, A15);
  or or_76 (or_76_out, A1, A2, A6);
  or or_77 (or_77_out, A2, A6, A9);
  or or_78 (or_78_out, B8, B6);
  or or_79 (or_79_out, A9, A11);
  or or_80 (or_80_out, B8, B9);
  or or_81 (or_81_out, B8, B15);
  or or_82 (or_82_out, B14, B0, B7);
  or or_83 (or_83_out, B6, B2);
  or or_84 (or_84_out, B6, B9);
  or or_85 (or_85_out, and_126_out, and_127_out);
  and and_128 (and_128_out, or_75_out, B9);
  and and_129 (and_129_out, A14, B8);
  and and_130 (and_130_out, or_76_out, B6);
  and and_131 (and_131_out, A9, B4);
  and and_132 (and_132_out, or_77_out, B2);
  and and_133 (and_133_out, or_78_out, A8);
  and and_134 (and_134_out, or_79_out, B9);
  and and_135 (and_135_out, A0, B0);
  and and_136 (and_136_out, or_80_out, A14);
  and and_137 (and_137_out, or_81_out, A8);
  and and_138 (and_138_out, or_82_out, A9);
  and and_139 (and_139_out, or_83_out, A2);
  and and_140 (and_140_out, or_84_out, A6);
  and and_141 (and_141_out, A1, B6);
  and and_142 (and_142_out, A15, B9);
  or or_86 (or_86_out, B8, B15, B9);
  or or_87 (or_87_out, B4, B14);
  or or_88 (or_88_out, A1, A8);
  or or_89 (or_89_out, B9, B2);
  T_Flip_Flop t_ff_21 (.clk(CP), .T(or_85_out), .Q(_22));  // open: Qn, preset, reset, en
  or or_90 (or_90_out, and_128_out, and_129_out, and_130_out, and_131_out, and_132_out);
  T_Flip_Flop t_ff_22 (.clk(CP), .T(or_91_out), .Q(_24));  // open: Qn, preset, reset, en
  or or_91 (or_91_out, and_133_out, and_134_out);
  or or_92 (or_92_out, and_135_out, and_136_out, and_137_out, and_138_out, and_140_out, and_141_out, and_142_out, and_139_out);
  or or_93 (or_93_out, B0, B9);
  or or_94 (or_94_out, B0, B4, B7, B14);
  and and_143 (and_143_out, or_94_out, A9);
  or or_95 (or_95_out, B2, B6);
  or or_96 (or_96_out, B0, B6, B15);
  and and_144 (and_144_out, A1, B6);
  and and_145 (and_145_out, or_86_out, A14);
  and and_146 (and_146_out, B9, A15);
  and and_147 (and_147_out, or_87_out, A9);
  and and_148 (and_148_out, or_88_out, B6);
  and and_149 (and_149_out, or_89_out, A6);
  and and_150 (and_150_out, A11, B9);
  and and_151 (and_151_out, A2, B15);
  T_Flip_Flop t_ff_23 (.clk(CP), .T(or_90_out), .Q(_23));  // open: Qn, preset, reset, en
  T_Flip_Flop t_ff_24 (.clk(CP), .T(or_92_out), .Q(_25));  // open: Qn, preset, reset, en
  and and_152 (and_152_out, A0, B0);
  and and_153 (and_153_out, or_93_out, A15);
  and and_154 (and_154_out, or_95_out, A2);
  and and_155 (and_155_out, or_96_out, A8);
  and and_156 (and_156_out, A14, B8);
  or or_97 (or_97_out, and_153_out, and_143_out, and_154_out, and_152_out, and_155_out, and_144_out, and_156_out);
  T_Flip_Flop t_ff_25 (.clk(CP), .T(or_98_out), .Q(_35));  // open: Qn, preset, reset, en
  or or_98 (or_98_out, and_145_out, and_146_out, and_147_out, and_148_out, and_149_out, and_150_out, and_151_out);
  or or_99 (or_99_out, B2, B0, B6);
  T_Flip_Flop t_ff_26 (.clk(CP), .T(or_97_out), .Q(_20));  // open: Qn, preset, reset, en
  or or_100 (or_100_out, A0, A8, A9);
  or or_101 (or_101_out, A2, A6, A9);
  or or_102 (or_102_out, A6, A11, A15);
  and and_157 (and_157_out, or_99_out, A9);
  or or_103 (or_103_out, A2, A6, A9);
  or or_104 (or_104_out, A2, A6);
  or or_105 (or_105_out, A15, A11, A6);
  or or_106 (or_106_out, A8, A9);
  or or_107 (or_107_out, A1, A9);
  or or_108 (or_108_out, A12, A11, A14);
  or or_109 (or_109_out, A8, A9);
  and and_158 (and_158_out, or_100_out, B0);
  and and_159 (and_159_out, or_101_out, B6);
  and and_160 (and_160_out, or_101_out, B2);
  and and_161 (and_161_out, or_102_out, B9);
  and and_162 (and_162_out, A2, B15);
  and and_163 (and_163_out, A14, B14);
  and and_164 (and_164_out, A14, B14);
  and and_165 (and_165_out, A8, B0);
  and and_166 (and_166_out, A11, B9);
  and and_167 (and_167_out, A14, B14);
  and and_168 (and_168_out, or_103_out, B2);
  and and_169 (and_169_out, or_104_out, B6);
  and and_170 (and_170_out, or_105_out, B9);
  and and_171 (and_171_out, B4, A9);
  and and_172 (and_172_out, or_106_out, B0);
  and and_173 (and_173_out, A14, B14);
  and and_174 (and_174_out, or_107_out, B6);
  and and_175 (and_175_out, or_108_out, B9);
  and and_176 (and_176_out, B8, A14);
  and and_177 (and_177_out, B2, A9);
  and and_178 (and_178_out, or_109_out, B0);
  or or_110 (or_110_out, and_158_out, and_159_out, and_160_out, and_161_out, and_162_out, and_163_out);
  T_Flip_Flop t_ff_27 (.clk(CP), .T(or_111_out), .Q(_27));  // open: Qn, preset, reset, en
  or or_111 (or_111_out, and_164_out, and_157_out, and_165_out, and_166_out);
  or or_112 (or_112_out, and_167_out, and_168_out, and_169_out, and_170_out, and_171_out, and_172_out);
  or or_113 (or_113_out, and_173_out, and_174_out, and_175_out, and_176_out, and_177_out, and_178_out);
  T_Flip_Flop t_ff_28 (.clk(CP), .T(or_110_out), .Q(_26));  // open: Qn, preset, reset, en
  T_Flip_Flop t_ff_29 (.clk(CP), .T(or_112_out), .Q(_28));  // open: Qn, preset, reset, en
  T_Flip_Flop t_ff_30 (.clk(CP), .T(or_113_out), .Q(_29));  // open: Qn, preset, reset, en
  nand nand_1 (nand_1_out, A15, B0);
  nand nand_2 (nand_2_out, A14, B15);
  nand nand_3 (nand_3_out, A8, B6);
  nand nand_4 (nand_4_out, A12, B9);
  nand nand_5 (nand_5_out, A9, B9);
  nand nand_6 (nand_6_out, A9, B0);
  nand nand_7 (nand_7_out, A9, B4);
  nand nand_8 (nand_8_out, A6, B2);
  nand nand_9 (nand_9_out, A2, B15);
  and and_179 (and_179_out, nand_1_out, nand_2_out, nand_3_out, nand_4_out, nand_5_out, nand_6_out, nand_7_out, nand_8_out, nand_9_out);
  T_Flip_Flop t_ff_31 (.clk(CP), .T(and_179_out), .Q(_30));  // open: Qn, preset, reset, en

  // Other names for the same wires on the sheet: _3 = _2; _4 = _2; _11 = _6; a = _16; b = _17; c = _18; d = _20;
  //   e = _31; _34 = _32; f = _32; g = _33; h = _35

  // Notes on the sheet:
  //   20BCE030
  //   20BCE031
  //   20BCE034
  //   DE - Innovative Assignment
  //   Group Roll numbers :
  //   Sequence Generators
  //   Title : Character Display Device
  //   Clock Pulse
  //   LED Display (Dot Matrix Display)
  //   Flip flop circuits :
  //   State Input Circuits :
  //   2,3,4
  //   6,11
  //   7
  //   16
  //   1
  //   5
  //   31
  //   8
  //   12
  //   13
  //   9
  //   10
  //   17
  //   32,34
  //   14
  //   15
  //   19
  //   21
  //   18
  //   33
  //   22
  //   35
  //   24
  //   23
  //   25
  //   20
  //   26
  //   27
  //   28
  //   29
  //   30
endmodule
